# Fritzing sketch Schematic (saved by Fritzing 0.9.3b)

parts:
  Part1 = Arduino Mega 2560 (Rev3)
  MCU1 = Raspberry Pi Zero

nets:
  N1: Part1.5V, MCU1.pin_2, MCU1.pin_4
  N2: Part1.D50, MCU1.pin_8
  N3: Part1.D52, MCU1.pin_6, MCU1.pin_39
